# Fritzing sketch fritzing (saved by Fritzing 0.9.2b)
breadboards: 1
perfboards: 1

parts:
  U1 = NodeMCU V1.0
  SD_card_module1 = SD Card Module
  Componente1 = Triple Axis Accelerometer Breakout - ADXL345
  R1 = Resistor [tolerance=±5% resistance=120 package=THT]
  R2 = Resistor [tolerance=±5% resistance=120 package=THT]
  R3 = Resistor [tolerance=±5% resistance=120 package=THT]
  R4 = Resistor [tolerance=±5% resistance=120 package=THT]
  J1 = female pin header, 2 pins [form="♀ (female)"]
  J2 = female pin header, 2 pins [form="♀ (female)"]
  J3 = female pin header, 2 pins [form="♀ (female)"]
  S1 = Pushbutton [package="[THT]"]
  S2 = Pushbutton [package="[THT]"]
  LED1 = LED - 5mm [color="Blue (470nm)" package="5 mm [THT]"]
  J4 = Piezo Speaker
  LED2 = LED - 5mm [color="White (4500K)" package="5 mm [THT]"]  # not connected
  Componente2 = Bluetooth HC-06
  Tiny_RTC1 = Tiny RTC

nets:
  N1: U1.D0, J2.pin1
  N2: U1.D1, Componente1.SDA, Tiny_RTC1.SDA
  N3: U1.D2, Componente1.SCL, Tiny_RTC1.SCL
  N4: U1.D3, J3.pin2
  N5: U1.D4, J3.pin1
  VCC: U1.3V3, SD_card_module1.+3.3, Componente1.VCC, Componente1.CS, J1.pin2, Tiny_RTC1.VCC
  GND: U1.GND, SD_card_module1.GND#7, Componente1.GND, J1.pin1, Componente2.GND, Tiny_RTC1.GND
  N6: U1.D5, SD_card_module1.SCK
  N7: U1.D6, SD_card_module1.MISO
  N8: U1.D7, SD_card_module1.MOSI
  N9: U1.D8, SD_card_module1.CS
  N10: U1.RX, Componente2.RXD
  N11: U1.TX, Componente2.TXD
  N12: U1.RSV, Componente2.VCC
  N13: U1.A0, J2.pin2
  N14: R1.Pin_0, S1.Pin_3, S1.Pin_4
  N15: R2.Pin_0, R3.Pin_0, R4.Pin_0
  N16: R2.Pin_1, R3.Pin_1, R4.Pin_1
  N17: S1.Pin_1, S1.Pin_2, S2.Pin_1, S2.Pin_2
  N18: S2.Pin_3, S2.Pin_4
  N19: LED1.cathode, J4.pin1
  N20: LED1.anode, J4.pin2

custom parts:
  NodeMCU V1.0: ESP8266 based NodeMCU
  SD Card Module: SD Card Module Slot Socket Reader For Arduino ARM MCU
  Tiny RTC: Tiny RTC I2C module DS1370Z RTC and AT24C32 EEPROM
